# Fritzing sketch Serial_monitor_Pull_up_circuits (saved by Fritzing 0.9.10b)
breadboards: 1

parts:
  Teensy1 = Teensy 4.0
  R1 = Resistor [tolerance=±5% power=0.25 resistance=220 package=THT]
  R2 = Resistor [tolerance=±5% power=0.25 resistance=220 package=THT]
  R3 = Resistor [tolerance=±5% power=0.25 resistance=220 package=THT]
  S1 = Pushbutton [package="[THT]"]
  S2 = Pushbutton [package="[THT]"]
  R4 = Resistor [tolerance=±5% power=0.25 resistance=220 package=THT]
  LED1 = RGB LED - (4 legs) [package="5 mm [THT]"]

nets:
  N1: Teensy1.pin_1, Teensy1.pin_9, Teensy1.pin_10, Teensy1.pin_32, S1.Pin_1, S1.Pin_2, S1.Pin_3, S1.Pin_4, S2.Pin_1, S2.Pin_2, S2.Pin_3, S2.Pin_4, LED1.common_anode
  N2: Teensy1.pin_26, R1.Pin_0
  N3: Teensy1.pin_29, R2.Pin_0
  N4: Teensy1.pin_30, R3.Pin_0
  N5: Teensy1.pin_31, R4.Pin_0
  N6: R1.Pin_1, LED1.red_cathode
  N7: R2.Pin_1, LED1.green_cathode
  N8: R3.Pin_1, LED1.blue_cathode

notes:
  CST8227-Interfacing
  Lab 04 - Pushbuttons to Control LED colors
  Control a tri-colorRBG with two switchs and a Pull-up resistor
  @Christopher Decarie-Dawson DECA0058

custom parts:
  Teensy 4.0: The Teensy is a complete USB-based microcontoller development system, in a very small footprint, capable of implementing many types of projects. All programming is done via the USB port. No special programmer is needed, only a standard micro-USB cable and a PC or Macintosh with a USB port.
